// Logisim project Full adder.circ as structural Verilog: 1 circuit, main circuit main
module main (
  input  Cin,
  input  A,
  input  B,
  output S,
  output Cout
);

  wire main_1_p3, main_1_p4, main_2_p4;

  // HalfAdder_main main_1: pin names not known; wires that end beside it: A, B, main_1_p3, main_1_p4
  // HalfAdder_main main_2: pin names not known; wires that end beside it: Cin, main_1_p3, S, main_2_p4
  or or_1 (Cout, main_2_p4, main_1_p4);
endmodule
