// Logisim project jk_circ.circ as structural Verilog: 1 circuit, main circuit main
module main (
  input  Reset,
  input  [3:0] Entrada_1,
  input  [3:0] Entrada_2,
  input  S,
  input  En_AB,
  input  S_Op,
  input  En_C
);

  wire Clock_out;
  wire [3:0] multiplexer_1_out, multiplexer_2_out, multiplexer_3_out, Reg_A_q, Reg_B_q, Reg_C_q, Soma_p3,
       Subtracao_p3;

  Clock Clock (.out(Clock_out));
  Multiplexer #(.width(4), .enable("false")) multiplexer_1 (
    .in0(Reg_C_q), .in1(Entrada_1), .out(multiplexer_1_out), .sel(S));
  Multiplexer #(.width(4), .enable("false")) multiplexer_2 (
    .in0(Reg_A_q), .in1(Entrada_2), .out(multiplexer_2_out), .sel(S));
  Register #(.width(4)) Reg_A (.D(multiplexer_1_out), .en(En_AB), .Q(Reg_A_q), .clk(Clock_out), .clr(Reset));
  Register #(.width(4)) Reg_B (.D(multiplexer_2_out), .en(En_AB), .Q(Reg_B_q), .clk(Clock_out), .clr(Reset));
  // Somatorio_main Soma: pin names not known; wires that end beside it: Reg_A_q, Reg_B_q, Soma_p3
  // Subtrator_main Subtracao: pin names not known; wires that end beside it: Reg_A_q, Reg_B_q, Subtracao_p3
  Multiplexer #(.width(4), .enable("false")) multiplexer_3 (
    .in0(Soma_p3), .in1(Subtracao_p3), .out(multiplexer_3_out), .sel(S_Op));
  Register #(.width(4)) Reg_C (.D(multiplexer_3_out), .en(En_C), .Q(Reg_C_q), .clk(Clock_out), .clr(Reset));

  // Notes on the sheet:
  //   0 = add e 1 = sub
endmodule
